// Logisim project Nanystec A1.circ as structural Verilog: 5 circuits, main circuit main
module main (
  output [7:0] out_1,
  output [7:0] out_2
);

  wire _1_1, adder_2_out, adder_3_out, adder_4_out, and_2_out, and_3_out, and_4_out, button_1_out,
       button_2_out, button_3_out, clock_1_out, Com, controlador_1_carregar_um_inteiro_imediato,
       controlador_1_jump, controlador_1_load, controlador_1_nada, controlador_1_out_7,
       controlador_1_se_r___1, controlador_1_shift_left, controlador_1_soma_inteiro, controlador_1_ssmd,
       controlador_1_storage, End, Erro___ou_minus, or_1_out, or_2_out, or_3_out, or_4_out, or_5_out,
       or_6_out, or_7_out, or_8_out, or_9_out, or_10_out, or_11_out, or_12_out, or_13_out, or_14_out,
       pulo_valor_1_erro_minus, pulo_valor_1_erro_plus, register_2_q, register_3_q, register_4_q;
  wire [2:0] controlador_1_aluf, multiplexer_1_out, multiplexer_2_out;
  wire [15:0] a1, AA, adder_1_out, alu_1_resultado, D1, D2, D3, multiplexer_4_out, multiplexer_5_out,
       multiplexer_6_out, pulo_valor_1_saida, ram_2_data, register_1_q;

  Adder #(.width(16)) adder_1 (.a(16'h1), .b(register_1_q), .out(adder_1_out));  // open: cin, cout
  and and_1 (Erro___ou_minus, or_1_out, or_2_out);
  Pulo_valor pulo_valor_1 (
    .PC(adder_1_out), .Jump({4'b0000, out_1[3:0], out_2}), .\Comparação ({{10{1'b0}}, out_2[5:0]}),
    .r___1({{7{1'b0}}, out_1[0], out_2}), .Saida(pulo_valor_1_saida), .Erro_plus(pulo_valor_1_erro_plus),
    .Erro_minus(pulo_valor_1_erro_minus), .jump_2(controlador_1_jump), .\comparações (and_2_out),
    .r___1_2(and_3_out));
  Register #(.width(16)) register_1 (
    .D(pulo_valor_1_saida), .Q(register_1_q), .clk(and_4_out), .clr(button_1_out));  // open: en
  Button button_1 (.out(button_1_out));
  or or_1 (or_1_out, controlador_1_se_r___1, controlador_1_out_7, controlador_1_jump);
  or or_2 (or_2_out, pulo_valor_1_erro_plus, pulo_valor_1_erro_minus);
  and and_2 (and_2_out, controlador_1_out_7, Com);
  and and_3 (and_3_out, controlador_1_se_r___1, _1_1);
  RAM #(.addrWidth(16), .dataWidth(16), .bus("asynch")) ram_1 (
    .addr(register_1_q), .data({out_1, out_2}));  // open: sel, ld, clr
  Adder #(.width(1)) adder_2 (.a(1'b1), .b(register_2_q), .out(adder_2_out));  // open: cin, cout
  Adder #(.width(1)) adder_3 (.a(1'b1), .b(register_3_q), .out(adder_3_out));  // open: cin, cout
  Button button_2 (.out(button_2_out));
  Register #(.width(1)) register_2 (.D(adder_2_out), .Q(register_2_q), .clk(or_3_out), .clr(button_3_out));  // open: en
  or or_3 (or_3_out, register_3_q, register_4_q);
  Register #(.width(1)) register_3 (.D(adder_3_out), .Q(register_3_q), .clk(End), .clr(button_3_out));  // open: en
  and and_4 (and_4_out, or_4_out, ~register_2_q);  // AND_Gate
  or or_4 (or_4_out, button_2_out, clock_1_out);
  Clock clock_1 (.out(clock_1_out));
  Button button_3 (.out(button_3_out));
  Adder #(.width(1)) adder_4 (.a(1'b1), .b(register_4_q), .out(adder_4_out));  // open: cin, cout
  Register #(.width(1)) register_4 (
    .D(adder_4_out), .Q(register_4_q), .clk(Erro___ou_minus), .clr(button_3_out));  // open: en
  Controlador controlador_1 (
    ._15(out_1[7]), ._14(out_1[6]), ._13(out_1[5]), ._12(out_1[4]), .Nada(controlador_1_nada),
    .SSMD(controlador_1_ssmd), .out_7(controlador_1_out_7), .ALUf(controlador_1_aluf),
    .Jump(controlador_1_jump), .Soma_Inteiro(controlador_1_soma_inteiro),
    .Carregar_um_inteiro_Imediato(controlador_1_carregar_um_inteiro_imediato),
    .Se_r___1(controlador_1_se_r___1), .End(End), .Shift_Left(controlador_1_shift_left),
    .Load(controlador_1_load), .Storage(controlador_1_storage));
  or or_5 (or_5_out, controlador_1_ssmd, controlador_1_shift_left, 1'b0);
  Multiplexer #(.width(3), .enable("false")) multiplexer_1 (
    .in0({out_1[0], out_2[7:6]}), .in1(out_2[5:3]), .out(multiplexer_1_out), .sel(or_5_out));
  or or_6 (or_6_out, controlador_1_carregar_um_inteiro_imediato, 1'b0);
  Multiplexer #(.width(3), .enable("false")) multiplexer_2 (
    .in0(multiplexer_1_out), .in1(out_1[3:1]), .out(multiplexer_2_out), .sel(or_6_out));
  or or_7 (or_7_out, controlador_1_ssmd, controlador_1_shift_left, controlador_1_soma_inteiro, 1'b0, controlador_1_load, controlador_1_carregar_um_inteiro_imediato);
  Multiplexer #(.width(16), .enable("false")) multiplexer_3 (
    .in0(multiplexer_6_out), .in1({{7{1'b0}}, out_1[0], out_2}), .out(D3), .sel(or_13_out));
  Registradores registradores_1 (
    .Registrador_1(out_1[3:1]), .Registrador_2({out_1[0], out_2[7:6]}),
    .Registrador_de_escrita(multiplexer_2_out), .Dados_de_escrita(D3), .Enable(or_7_out), .Clock(and_4_out),
    .Valor_de_a1(a1), .Dados_1(D1), .Dados2(D2));
  Hex_Digit_Display hex_digit_display_1 (.value(D1[15:12]));  // open: dp
  or or_8 (or_8_out, controlador_1_load, controlador_1_storage, 1'b0, controlador_1_soma_inteiro);
  Shifter #(.width(16)) shifter_1 (.in(D1), .\dist ({1'b0, out_2[2:0]}), .out(AA));
  Hex_Digit_Display hex_digit_display_2 (.value(D1[11:8]));  // open: dp
  Hex_Digit_Display hex_digit_display_3 (.value(D1[7:4]));  // open: dp
  Hex_Digit_Display hex_digit_display_4 (.value(D3[15:12]));  // open: dp
  Multiplexer #(.width(16), .enable("false")) multiplexer_4 (
    .in0(D2), .in1({{10{1'b0}}, out_2[5:0]}), .out(multiplexer_4_out), .sel(or_8_out));
  Hex_Digit_Display hex_digit_display_5 (.value(D1[3:0]));  // open: dp
  Hex_Digit_Display hex_digit_display_6 (.value(D3[7:4]));  // open: dp
  Hex_Digit_Display hex_digit_display_7 (.value(D3[11:8]));  // open: dp
  or or_9 (or_9_out, controlador_1_se_r___1, 1'b0);
  ALU alu_1 (
    .Entrada_1(D1), .Entrada_2(multiplexer_4_out), .\Operação (controlador_1_aluf), .compara_pula(or_9_out),
    ._1_1_pulo_R(_1_1), .resu_1_bit(Com), .Resultado(alu_1_resultado));
  Hex_Digit_Display hex_digit_display_8 (.value(D2[11:8]));  // open: dp
  Hex_Digit_Display hex_digit_display_9 (.value(D2[15:12]));  // open: dp
  Hex_Digit_Display hex_digit_display_10 (.value(D3[3:0]));  // open: dp
  or or_10 (or_10_out, controlador_1_storage, 1'b0);
  Hex_Digit_Display hex_digit_display_11 (.value(D2[3:0]));  // open: dp
  Hex_Digit_Display hex_digit_display_12 (.value(D2[7:4]));  // open: dp
  or or_11 (or_11_out, controlador_1_load, 1'b0);
  RAM #(.addrWidth(16), .dataWidth(16), .bus("separate")) ram_2 (
    .addr(alu_1_resultado), .din(D2), .data(ram_2_data), .str(or_10_out), .clk(and_4_out), .ld(or_11_out));  // open: sel, clr
  Hex_Digit_Display hex_digit_display_13 (.value(a1[11:8]));  // open: dp
  Hex_Digit_Display hex_digit_display_14 (.value(a1[15:12]));  // open: dp
  or or_12 (or_12_out, controlador_1_load, 1'b0);
  or or_13 (or_13_out, controlador_1_carregar_um_inteiro_imediato, 1'b0);
  Multiplexer #(.width(16), .enable("false")) multiplexer_5 (
    .in0(alu_1_resultado), .in1(ram_2_data), .out(multiplexer_5_out), .sel(or_12_out));
  Hex_Digit_Display hex_digit_display_15 (.value(a1[7:4]));  // open: dp
  Hex_Digit_Display hex_digit_display_16 (.value(a1[3:0]));  // open: dp
  or or_14 (or_14_out, controlador_1_shift_left, 1'b0);
  Multiplexer #(.width(16), .enable("false")) multiplexer_6 (
    .in0(multiplexer_5_out), .in1(AA), .out(multiplexer_6_out), .sel(or_14_out));

  // Other names for the same wires on the sheet: _0 = out_2[0]; Endereço[5:0] = out_2[5:0];
  //   Endereço_9_bits[8:0] = {out_1[0], out_2}; Jump[11:0] = {out_1[3:0], out_2}; _1 = out_2[1]; _2 = out_2[2];
  //   _3 = out_2[3]; _4 = out_2[4]; _5 = out_2[5]

  // Notes on the sheet:
  //   o segundo desgitrador que vai ser usado
  //   e o total de shifts lefts é os ultimos tres bits
  //   Comparações
endmodule

module Controlador (
  input  _15,
  input  _14,
  input  _13,
  input  _12,
  output Nada,
  output SSMD,
  output out_7,
  output [2:0] ALUf,
  output Jump,
  output Soma_Inteiro,
  output Carregar_um_inteiro_Imediato,
  output Se_r___1,
  output End,
  output Shift_Left,
  output Load,
  output Storage
);

  wire _0001, _0010, _0011, _0100, _0101, _0110, _0111, _1000, _1001, _1010, _1011, _1100, _1101, _1110,
       _1111, or_9_out;
  wire [2:0] multiplexer_1_out, multiplexer_2_out, multiplexer_3_out, multiplexer_4_out, multiplexer_5_out,
       multiplexer_6_out, multiplexer_7_out, multiplexer_8_out;

  and and_1 (_1111, _15, _14, _13, _12);
  and and_2 (_0111, ~_15, _14, _13, _12);  // AND_Gate
  and and_3 (_1011, _15, ~_14, _13, _12);  // AND_Gate
  and and_4 (_0011, ~_15, ~_14, _13, _12);  // AND_Gate
  and and_5 (_1101, _15, _14, ~_13, _12);  // AND_Gate
  and and_6 (_0101, ~_15, _14, ~_13, _12);  // AND_Gate
  and and_7 (_1001, _15, ~_14, ~_13, _12);  // AND_Gate
  and and_8 (_0001, ~_15, ~_14, ~_13, _12);  // AND_Gate
  and and_9 (_1110, _15, _14, _13, ~_12);  // AND_Gate
  and and_10 (_0110, ~_15, _14, _13, ~_12);  // AND_Gate
  and and_11 (_1010, _15, ~_14, _13, ~_12);  // AND_Gate
  and and_12 (_0010, ~_15, ~_14, _13, ~_12);  // AND_Gate
  and and_13 (_1100, _15, _14, ~_13, ~_12);  // AND_Gate
  and and_14 (_0100, ~_15, _14, ~_13, ~_12);  // AND_Gate
  and and_15 (_1000, _15, ~_14, ~_13, ~_12);  // AND_Gate
  and and_16 (Nada, ~_15, ~_14, ~_13, ~_12);  // AND_Gate
  Multiplexer #(.width(3), .enable("false")) multiplexer_1 (
    .in0(3'b000), .in1(3'b100), .out(multiplexer_1_out), .sel(_0001));
  Multiplexer #(.width(3), .enable("false")) multiplexer_2 (
    .in0(multiplexer_1_out), .in1(3'b101), .out(multiplexer_2_out), .sel(_0010));
  Multiplexer #(.width(3), .enable("false")) multiplexer_3 (
    .in0(multiplexer_2_out), .in1(3'b110), .out(multiplexer_3_out), .sel(_0011));
  Multiplexer #(.width(3), .enable("false")) multiplexer_4 (
    .in0(multiplexer_3_out), .in1(3'b111), .out(multiplexer_4_out), .sel(_0100));
  or or_1 (Jump, _1000, 1'b0);
  or or_2 (Soma_Inteiro, _1001, 1'b0);
  or or_3 (Carregar_um_inteiro_Imediato, _1010, 1'b0);
  or or_4 (Se_r___1, _1011, 1'b0);
  or or_5 (End, _1100, 1'b0);
  or or_6 (Shift_Left, _1101, 1'b0);
  or or_7 (Load, _1110, 1'b0);
  or or_8 (Storage, _1111, 1'b0);
  Multiplexer #(.width(3), .enable("false")) multiplexer_5 (
    .in0(multiplexer_4_out), .in1(3'b001), .out(multiplexer_5_out), .sel(_0101));
  Multiplexer #(.width(3), .enable("false")) multiplexer_6 (
    .in0(multiplexer_5_out), .in1(3'b010), .out(multiplexer_6_out), .sel(_0110));
  Multiplexer #(.width(3), .enable("false")) multiplexer_7 (
    .in0(multiplexer_6_out), .in1(3'b011), .out(multiplexer_7_out), .sel(_0111));
  Multiplexer #(.width(3), .enable("false")) multiplexer_8 (
    .in0(multiplexer_7_out), .in1(3'b100), .out(multiplexer_8_out), .sel(or_9_out));
  or or_9 (or_9_out, _1001, _1110, _1111);
  or or_10 (SSMD, _0001, _0010, _0011, _0100);
  or or_11 (out_7, _0101, _0110, _0111);
  Multiplexer #(.width(3), .enable("false")) multiplexer_9 (
    .in0(multiplexer_8_out), .in1(3'b001), .out(ALUf), .sel(_1011));
  Button button_1 ();  // open: out

  // Other names for the same wires on the sheet: _0000 = Nada

  // Notes on the sheet:
  //   multiplicação
  //   =
  //   <
  //   >
  //   soma
  //   subtração
  //   divisão
endmodule

module ALU (
  input  [2:0] \Operação ,
  input  compara_pula,
  input  [15:0] Entrada_1,
  input  [15:0] Entrada_2,
  output _1_1_pulo_R,
  output resu_1_bit,
  output [15:0] Resultado
);

  wire comparator_1_eq, comparator_2_lt, comparator_3_gt, multiplexer_3_out;
  wire [15:0] adder_1_out, divider_1_out, multiplexer_1_out, multiplexer_2_out, multiplier_1_out,
       subtractor_1_out;

  Multiplexer #(.width(16), .enable("false")) multiplexer_1 (
    .in0(Entrada_2), .in1(16'h1), .out(multiplexer_1_out), .sel(compara_pula));
  Adder #(.width(16)) adder_1 (.a(Entrada_1), .b(multiplexer_1_out), .out(adder_1_out));  // open: cin, cout
  Subtractor #(.width(16)) subtractor_1 (
    .a(Entrada_1), .b(multiplexer_1_out), .out(subtractor_1_out));  // open: bin, bout
  Multiplier #(.width(16)) multiplier_1 (
    .a(Entrada_1), .b(multiplexer_1_out), .out(multiplier_1_out));  // open: cin, cout
  Divider #(.width(16)) divider_1 (.a(Entrada_1), .b(multiplexer_1_out), .out(divider_1_out));  // open: upper, rem
  Comparator #(.width(16)) comparator_1 (.a(Entrada_1), .b(multiplexer_1_out), .eq(comparator_1_eq));  // open: gt, lt
  Comparator #(.width(16)) comparator_2 (.a(Entrada_1), .b(multiplexer_1_out), .lt(comparator_2_lt));  // open: gt, eq
  Comparator #(.width(16)) comparator_3 (.a(Entrada_1), .b(multiplexer_1_out), .gt(comparator_3_gt));  // open: eq, lt
  Multiplexer #(.select(3), .width(16), .enable("false")) multiplexer_2 (
    .in0({16{1'b0}}), .in1({16{1'b0}}), .in2({16{1'b0}}), .in3({16{1'b0}}), .in4(adder_1_out),
    .in5(subtractor_1_out), .in6(multiplier_1_out), .in7(divider_1_out), .out(multiplexer_2_out),
    .sel(\Operação ));
  Multiplexer #(.select(3), .enable("false")) multiplexer_3 (
    .in0(1'b0), .in1(comparator_1_eq), .in2(comparator_2_lt), .in3(comparator_3_gt), .in4(1'b0), .in5(1'b0),
    .in6(1'b0), .in7(1'b0), .out(multiplexer_3_out), .sel(\Operação ));
  and and_1 (_1_1_pulo_R, compara_pula, multiplexer_3_out);
  and and_2 (resu_1_bit, ~compara_pula, multiplexer_3_out);  // AND_Gate
  Multiplexer #(.width(16), .enable("false")) multiplexer_4 (
    .in0(multiplexer_2_out), .in1({16{1'b0}}), .out(Resultado), .sel(resu_1_bit));
  Button button_1 ();  // open: out

  // Other names for the same wires on the sheet: opera[2:0] = \Operação 
endmodule

module Registradores (
  input  Enable,
  input  [2:0] Registrador_1,
  input  [2:0] Registrador_2,
  input  [2:0] Registrador_de_escrita,
  input  Clock,
  input  [15:0] Dados_de_escrita,
  output [15:0] Dados_1,
  output [15:0] Dados2,
  output [15:0] Valor_de_a1
);

  wire demultiplexer_1_out1, demultiplexer_1_out2, demultiplexer_1_out3, demultiplexer_1_out4,
       demultiplexer_1_out5, demultiplexer_1_out6, demultiplexer_1_out7;
  wire [15:0] demultiplexer_2_out1, demultiplexer_2_out2, demultiplexer_2_out3, demultiplexer_2_out4,
       demultiplexer_2_out5, demultiplexer_2_out6, demultiplexer_2_out7, register_1_q, register_3_q,
       register_4_q, register_5_q, register_6_q, register_7_q, register_8_q;

  Demultiplexer #(.select(3), .enable("false")) demultiplexer_1 (
    .out1(demultiplexer_1_out1), .out2(demultiplexer_1_out2), .out3(demultiplexer_1_out3),
    .out4(demultiplexer_1_out4), .out5(demultiplexer_1_out5), .out6(demultiplexer_1_out6),
    .out7(demultiplexer_1_out7), .in(Enable), .sel(Registrador_de_escrita));  // open: out0
  Demultiplexer #(.select(3), .width(16), .enable("false")) demultiplexer_2 (
    .out1(demultiplexer_2_out1), .out2(demultiplexer_2_out2), .out3(demultiplexer_2_out3),
    .out4(demultiplexer_2_out4), .out5(demultiplexer_2_out5), .out6(demultiplexer_2_out6),
    .out7(demultiplexer_2_out7), .in(Dados_de_escrita), .sel(Registrador_de_escrita));  // open: out0
  Register #(.width(16)) register_1 (.Q(register_1_q), .clk(Clock));  // open: D, en, clr
  Register #(.width(16)) register_2 (
    .D(demultiplexer_2_out1), .en(demultiplexer_1_out1), .Q(Valor_de_a1), .clk(Clock));  // open: clr
  Register #(.width(16)) register_3 (
    .D(demultiplexer_2_out2), .en(demultiplexer_1_out2), .Q(register_3_q), .clk(Clock));  // open: clr
  Register #(.width(16)) register_4 (
    .D(demultiplexer_2_out3), .en(demultiplexer_1_out3), .Q(register_4_q), .clk(Clock));  // open: clr
  Register #(.width(16)) register_5 (
    .D(demultiplexer_2_out4), .en(demultiplexer_1_out4), .Q(register_5_q), .clk(Clock));  // open: clr
  Register #(.width(16)) register_6 (
    .D(demultiplexer_2_out5), .en(demultiplexer_1_out5), .Q(register_6_q), .clk(Clock));  // open: clr
  Register #(.width(16)) register_7 (
    .D(demultiplexer_2_out6), .en(demultiplexer_1_out6), .Q(register_7_q), .clk(Clock));  // open: clr
  Register #(.width(16)) register_8 (
    .D(demultiplexer_2_out7), .en(demultiplexer_1_out7), .Q(register_8_q), .clk(Clock));  // open: clr
  Multiplexer #(.select(3), .width(16), .enable("false")) multiplexer_1 (
    .in0(register_1_q), .in1(Valor_de_a1), .in2(register_3_q), .in3(register_4_q), .in4(register_5_q),
    .in5(register_6_q), .in6(register_7_q), .in7(register_8_q), .out(Dados_1), .sel(Registrador_1));
  Multiplexer #(.select(3), .width(16), .enable("false")) multiplexer_2 (
    .in0(register_1_q), .in1(Valor_de_a1), .in2(register_3_q), .in3(register_4_q), .in4(register_5_q),
    .in5(register_6_q), .in6(register_7_q), .in7(register_8_q), .out(Dados2), .sel(Registrador_2));
  Button button_1 ();  // open: out

  // Other names for the same wires on the sheet: Reg_1[2:0] = Registrador_1; Reg_2[2:0] = Registrador_2

  // Notes on the sheet:
  //   Registrador 0 sempre
  //   $0
  //   $a1
  //   $r1
  //   $r2
  //   $t1
  //   $t2
  //   $t3
  //   $t4
endmodule

module Pulo_valor (
  input  [15:0] Jump,
  input  [15:0] \Comparação ,
  input  [15:0] r___1,
  input  [15:0] PC,
  input  jump_2,
  input  \comparações ,
  input  r___1_2,
  output Erro_plus,
  output Erro_minus,
  output [15:0] Saida
);

  wire adder_4_cout, adder_5_cout, adder_6_cout, and_1_out, and_2_out, and_3_out, and_4_out, and_5_out,
       and_6_out, and_7_out, and_8_out, and_9_out, and_10_out, and_11_out, and_12_out, not_1_out, or_1_out,
       or_2_out, or_3_out, or_4_out, or_5_out, subtractor_4_bout, subtractor_5_bout, subtractor_6_bout;
  wire [15:0] adder_1_out, adder_2_out, adder_3_out, adder_4_out, adder_5_out, adder_6_out,
       multiplexer_1_out, multiplexer_2_out, multiplexer_3_out, multiplexer_5_out, multiplexer_6_out,
       multiplexer_7_out, multiplexer_8_out, multiplexer_9_out, multiplexer_10_out, multiplexer_11_out,
       multiplexer_12_out, multiplexer_13_out, subtractor_1_out, subtractor_2_out, subtractor_3_out,
       subtractor_4_out, subtractor_5_out, subtractor_6_out;

  Multiplexer #(.width(16), .enable("false")) multiplexer_1 (
    .in0(PC), .in1(multiplexer_5_out), .out(multiplexer_1_out), .sel(or_3_out));
  Multiplexer #(.width(16), .enable("false")) multiplexer_2 (
    .in0(multiplexer_1_out), .in1(multiplexer_8_out), .out(multiplexer_2_out), .sel(or_4_out));
  Multiplexer #(.width(16), .enable("false")) multiplexer_3 (
    .in0(multiplexer_2_out), .in1(multiplexer_11_out), .out(multiplexer_3_out), .sel(or_5_out));
  Multiplexer #(.width(16), .enable("false")) multiplexer_4 (
    .in0(multiplexer_3_out), .in1(PC), .out(Saida), .sel(not_1_out));
  Multiplexer #(.width(16), .enable("false")) multiplexer_5 (
    .in0(adder_6_out), .in1(subtractor_6_out), .out(multiplexer_5_out), .sel(Jump[11]));
  Subtractor #(.width(16)) subtractor_1 (
    .a({{5{1'b0}}, Jump[10:0]}), .b(16'h1), .out(subtractor_1_out));  // open: bin, bout
  Multiplexer #(.width(16), .enable("false")) multiplexer_6 (
    .in0({16{1'b0}}), .in1(subtractor_1_out), .out(multiplexer_6_out), .sel(jump_2));
  Adder #(.width(16)) adder_1 (.a({{5{1'b0}}, Jump[10:0]}), .b(16'h1), .out(adder_1_out));  // open: cin, cout
  Multiplexer #(.width(16), .enable("false")) multiplexer_7 (
    .in0({16{1'b0}}), .in1(adder_1_out), .out(multiplexer_7_out), .sel(jump_2));
  Multiplexer #(.width(16), .enable("false")) multiplexer_8 (
    .in0(adder_5_out), .in1(subtractor_5_out), .out(multiplexer_8_out), .sel(\Comparação [5]));
  Adder #(.width(16)) adder_2 (.a({{11{1'b0}}, \Comparação [4:0]}), .b(16'h1), .out(adder_2_out));  // open: cin, cout
  Subtractor #(.width(16)) subtractor_2 (
    .a({{11{1'b0}}, \Comparação [4:0]}), .b(16'h1), .out(subtractor_2_out));  // open: bin, bout
  Multiplexer #(.width(16), .enable("false")) multiplexer_9 (
    .in0({16{1'b0}}), .in1(subtractor_2_out), .out(multiplexer_9_out), .sel(\comparações ));
  Multiplexer #(.width(16), .enable("false")) multiplexer_10 (
    .in0({16{1'b0}}), .in1(adder_2_out), .out(multiplexer_10_out), .sel(\comparações ));
  Multiplexer #(.width(16), .enable("false")) multiplexer_11 (
    .in0(adder_4_out), .in1(subtractor_4_out), .out(multiplexer_11_out), .sel(r___1[8]));
  Subtractor #(.width(16)) subtractor_3 (
    .a({{8{1'b0}}, r___1[7:0]}), .b(16'h1), .out(subtractor_3_out));  // open: bin, bout
  Adder #(.width(16)) adder_3 (.a({{8{1'b0}}, r___1[7:0]}), .b(16'h1), .out(adder_3_out));  // open: cin, cout
  Multiplexer #(.width(16), .enable("false")) multiplexer_12 (
    .in0({16{1'b0}}), .in1(adder_3_out), .out(multiplexer_12_out), .sel(r___1_2));
  Multiplexer #(.width(16), .enable("false")) multiplexer_13 (
    .in0({16{1'b0}}), .in1(subtractor_3_out), .out(multiplexer_13_out), .sel(r___1_2));
  Adder #(.width(16)) adder_4 (.a(PC), .b(multiplexer_13_out), .out(adder_4_out), .cout(adder_4_cout));  // open: cin
  Adder #(.width(16)) adder_5 (.a(PC), .b(multiplexer_9_out), .out(adder_5_out), .cout(adder_5_cout));  // open: cin
  Adder #(.width(16)) adder_6 (.a(PC), .b(multiplexer_6_out), .out(adder_6_out), .cout(adder_6_cout));  // open: cin
  Subtractor #(.width(16)) subtractor_4 (
    .a(PC), .b(multiplexer_12_out), .out(subtractor_4_out), .bout(subtractor_4_bout));  // open: bin
  Subtractor #(.width(16)) subtractor_5 (
    .a(PC), .b(multiplexer_10_out), .out(subtractor_5_out), .bout(subtractor_5_bout));  // open: bin
  Subtractor #(.width(16)) subtractor_6 (
    .a(PC), .b(multiplexer_7_out), .out(subtractor_6_out), .bout(subtractor_6_bout));  // open: bin
  or or_1 (or_1_out, Jump[11], \Comparação [5], r___1[8]);
  and and_1 (and_1_out, or_1_out, subtractor_4_bout);
  and and_2 (and_2_out, or_1_out, subtractor_5_bout);
  and and_3 (and_3_out, or_1_out, subtractor_6_bout);
  or or_2 (or_2_out, or_3_out, or_4_out, or_5_out);
  not not_1 (not_1_out, or_2_out);
  and and_4 (and_4_out, ~or_1_out, adder_4_cout);  // AND_Gate
  and and_5 (and_5_out, ~or_1_out, adder_5_cout);  // AND_Gate
  and and_6 (and_6_out, ~or_1_out, adder_6_cout);  // AND_Gate
  or or_3 (or_3_out, 1'b0, jump_2);
  or or_4 (or_4_out, 1'b0, \comparações );
  or or_5 (or_5_out, 1'b0, r___1_2);
  and and_7 (and_7_out, and_4_out, jump_2);
  or or_6 (Erro_plus, and_7_out, and_8_out, and_9_out);
  and and_8 (and_8_out, and_5_out, \comparações );
  and and_9 (and_9_out, and_6_out, r___1_2);
  and and_10 (and_10_out, and_1_out, jump_2);
  and and_11 (and_11_out, and_2_out, \comparações );
  and and_12 (and_12_out, and_3_out, r___1_2);
  or or_7 (Erro_minus, and_10_out, and_11_out, and_12_out);
  Button button_1 ();  // open: out

  // Other names for the same wires on the sheet: Comparação_t = \comparações ; Jump_t = jump_2; r___1_t = r___1_2

  // Notes on the sheet:
  //   Jump 1 + 11
  //   Comparação 1 + 5
  //   r = 1 1+ 8
endmodule
